# Fritzing sketch CircuitDiagram_1 (saved by Fritzing 0.9.3b)
breadboards: 1

parts:
  元件1 = Arduino Nano (Rev3.0)
  R1 = Basic Flex Resistor
  R2 = Basic Flex Resistor
  R3 = Basic Flex Resistor
  R4 = Basic Flex Resistor
  R5 = Basic Flex Resistor
  R11 = Resistor [tolerance=±5% resistance=20k package=THT]
  R12 = Resistor [tolerance=±5% resistance=20k package=THT]
  R13 = Resistor [tolerance=±5% resistance=20k package=THT]
  R14 = Resistor [tolerance=±5% resistance=20k package=THT]
  R15 = Resistor [tolerance=±5% resistance=220 package=THT]

nets:
  N1: 元件1.GND, R11.Pin_1, R12.Pin_1, R13.Pin_1, R14.Pin_1, R15.Pin_1
  N2: 元件1.5V, R1.pin_1, R2.pin_1, R3.pin_1, R4.pin_1, R5.pin_1
  N3: 元件1.A4, R5.Pin_2, R15.Pin_0
  N4: 元件1.A3, R4.Pin_2, R14.Pin_0
  N5: 元件1.A2, R3.Pin_2, R13.Pin_0
  N6: 元件1.A1, R2.Pin_2, R12.Pin_0
  N7: 元件1.A0, R1.Pin_2, R11.Pin_0
